// Logisim project project3.circ as structural Verilog: 6 circuits, main circuit ALU
module ALU (
  input  [3:0] FunSel,
  input  C_in,
  input  [7:0] A,
  input  [7:0] B,
  output [3:0] ZCNO,
  output [7:0] out_6
);

  wire and_2_out, and_3_out, and_4_out, and_5_out, C, C1, C2, C3, clock_1_out, N, O, O1, O2, O3, O10,
       xor_3_out, Z;
  wire [31:0] ALU_MUX_4_7;
  wire [31:8] ALU_MUX_0_3;
  wire [31:24] ALU_MUX_12_15;

  xor xor_1 (O10, A[6], A[7]);
  assign ALU_MUX_12_15 = ~B;  // NOT_Gate not_1, 8 bits wide
  Adder adder_1 (.a(A), .b(B), .out(ALU_MUX_0_3[15:8]), .cout(C1));  // open: cin
  Adder adder_2 (.a(A), .b(B), .out(ALU_MUX_0_3[23:16]), .cin(C_in), .cout(C2));
  Subtractor subtractor_1 (.a(A), .b(B), .out(ALU_MUX_0_3[31:24]), .bout(C3));  // open: bin
  assign ALU_MUX_4_7[7:0] = A & B;  // AND_Gate and_1, 8 bits wide
  assign ALU_MUX_4_7[15:8] = A | B;  // OR_Gate or_1, 8 bits wide
  assign ALU_MUX_4_7[23:16] = ~A;  // NOT_Gate not_2, 8 bits wide
  assign ALU_MUX_4_7[31:24] = A ^ B;  // XOR_Gate xor_2, 8 bits wide
  Multiplexer #(.select(4), .enable("false")) multiplexer_1 (
    .in1(C1), .in2(C2), .in3(C3), .in8(A[7]), .in9(A[0]), .in12(A[7]), .in13(A[0]), .out(C), .sel(FunSel));  // open: in0, in4, in5, in6, in7, in10, in11, in14, in15
  and and_2 (and_2_out, ~A[7], B[7], out_6[7]);  // AND_Gate
  and and_3 (and_3_out, A[7], ~B[7], ~out_6[7]);  // AND_Gate
  and and_4 (and_4_out, ~out_6[7], A[7], B[7]);  // AND_Gate
  and and_5 (and_5_out, out_6[7], ~A[7], ~B[7]);  // AND_Gate
  Multiplexer #(.select(4), .width(8), .enable("false")) multiplexer_2 (
    .in0(A), .in1(ALU_MUX_0_3[15:8]), .in2(ALU_MUX_0_3[23:16]), .in3(ALU_MUX_0_3[31:24]),
    .in4(ALU_MUX_4_7[7:0]), .in5(ALU_MUX_4_7[15:8]), .in6(ALU_MUX_4_7[23:16]), .in7(ALU_MUX_4_7[31:24]),
    .in8({A[6:0], 1'b0}), .in9({1'b0, A[7:1]}), .in10({A[6:0], 1'b0}), .in11({{2{A[7]}}, A[6:1]}),
    .in12({A[6:0], A[7]}), .in13({A[0], A[7:1]}), .in14(B), .in15(ALU_MUX_12_15), .out(out_6), .sel(FunSel));
  or or_2 (O3, and_2_out, and_3_out);
  or or_3 (O1, and_4_out, and_5_out);
  xor xor_3 (xor_3_out, C_in, C2);
  Multiplexer #(.select(4), .enable("false")) multiplexer_3 (
    .in1(O1), .in2(O2), .in3(O3), .in10(O10), .in11(1'b0), .in12(1'b0), .in13(1'b0), .out(O), .sel(FunSel));  // open: in0, in4, in5, in6, in7, in8, in9, in14, in15
  Clock clock_1 (.out(clock_1_out));
  or or_4 (O2, O1, xor_3_out);
  Multiplexer #(.select(4), .enable("false")) multiplexer_4 (
    .in0(out_6[7]), .in1(out_6[7]), .in2(out_6[7]), .in3(out_6[7]), .in4(out_6[7]), .in5(out_6[7]),
    .in6(out_6[7]), .in7(out_6[7]), .in8(out_6[7]), .in9(out_6[7]), .in11(out_6[7]), .in12(out_6[7]),
    .in13(out_6[7]), .in14(out_6[7]), .in15(out_6[7]), .out(N), .sel(FunSel));  // open: in10
  D_Flip_Flop d_ff_1 (.clk(clock_1_out), .D(C), .Q(ZCNO[2]), .en(1'b1));  // open: Qn, preset, reset
  D_Flip_Flop d_ff_2 (.clk(clock_1_out), .D(N), .Q(ZCNO[1]), .en(1'b1));  // open: Qn, preset, reset
  D_Flip_Flop d_ff_3 (.clk(clock_1_out), .D(O), .Q(ZCNO[0]), .en(1'b1));  // open: Qn, preset, reset
  nor nor_1 (Z, out_6[0], out_6[1], out_6[2], out_6[3], out_6[4], out_6[5], out_6[6], out_6[7]);
  D_Flip_Flop d_ff_4 (.clk(clock_1_out), .D(Z), .Q(ZCNO[3]), .en(1'b1));  // open: Qn, preset, reset

  // Other names for the same wires on the sheet: ALU_MUX_0_3[7:0] = A;
  //   ALU_MUX_8_11 (some bits) = {{2{A[7]}}, A[6:1], A[6:0], A[7:1], A[6:0]};
  //   ALU_MUX_12_15[23:0] = {B, A[0], A[7:1], A[6:0], A[7]}; C9 = A[0]; C13 = A[0]; C8 = A[7]; C12 = A[7]; Cin = C_in;
  //   OUT7 = out_6[7]

  // Notes on the sheet:
  //   CARRY
  //   ALU
  //   OVERFLOW
  //    = A7'.B7.OUT7 + A7.B7'.OUT7'
  //   =A7.B7.OUT7' + A7'.B7'.OUT7
  //   =(Cin (XOR) C2) + O1 
  //   NEGATIVE
  //   OUTPUT
endmodule

module Basic_Computer (
  output [7:0] out_1,
  output [3:0] out_2,
  output [7:0] out_3
);

  wire ASELALU, BSELALU, CLOCK_out, IR_EN, IRL_H_prime, MEMLD, MEMMUXSEL, MEMSTR;
  wire [1:0] AMUXSEL, ARFFUNSEL, BMUXSEL, IRFUNSEL, OUTASEL, OUTBSEL, OUTCSEL, OUTDSEL, RFFUNSEL;
  wire [2:0] ARFREGSEL;
  wire [3:0] alu_1_zcno, FUNSELALU, RFREGSEL;
  wire [7:0] IROUT, multiplexer_1_out, multiplexer_2_out, multiplexer_3_out, multiplexer_4_out,
       multiplexer_5_out, n8_bit_register_file_1_out_6, n8_bit_register_file_1_out_7, pc_ar_sp_1_out_6,
       pc_ar_sp_1_out_7, ram_1_data;

  Multiplexer #(.select(2), .width(8), .enable("false")) multiplexer_1 (
    .in0(out_1), .in1(pc_ar_sp_1_out_6), .in2(ram_1_data), .in3(IROUT), .out(multiplexer_1_out), .sel(AMUXSEL));
  _8_bit_Register_File u_8_bit_register_file_1 (
    .RegSel(RFREGSEL), .FunSel(RFFUNSEL), .in_1(multiplexer_1_out), .OutASel(OUTASEL), .OutBSel(OUTBSEL),
    .out_6(n8_bit_register_file_1_out_6), .out_7(n8_bit_register_file_1_out_7));
  _16_bit_IR_Register u_16_bit_ir_register_1 (
    .L_H(IRL_H_prime), .Input(ram_1_data), .in_2(IRFUNSEL), .in_3(IR_EN), .out_5({out_3, IROUT}));
  Multiplexer #(.width(8), .enable("false")) multiplexer_2 (
    .in0(n8_bit_register_file_1_out_6), .in1(pc_ar_sp_1_out_7), .out(multiplexer_2_out), .sel(ASELALU));
  Multiplexer #(.width(8), .enable("false")) multiplexer_3 (
    .in0(n8_bit_register_file_1_out_7), .in1(pc_ar_sp_1_out_6), .out(multiplexer_3_out), .sel(BSELALU));
  Multiplexer #(.select(2), .width(8), .enable("false")) multiplexer_4 (
    .in0(out_1), .in1(IROUT), .in2(ram_1_data), .in3(pc_ar_sp_1_out_6), .out(multiplexer_4_out), .sel(BMUXSEL));
  Control_Unit control_unit_1 (
    .LD_M(MEMLD), .out_4(BSELALU), .IR_EN(IR_EN), .IRL_H(IRL_H_prime), .MEMSTR(MEMSTR), .out_8(ASELALU),
    .FUNSELALU(FUNSELALU), .out_10(AMUXSEL), .out_11(MEMMUXSEL), .out_12(OUTBSEL), .out_13(BMUXSEL),
    .RFFUNSEL(RFFUNSEL), .out_15(OUTCSEL), .OUTASEL(OUTASEL), .out_17(ARFFUNSEL), .out_18(OUTDSEL),
    .out_19(RFREGSEL), .out_20(ARFREGSEL), .out_21(IRFUNSEL), .in_1({out_3, IROUT}), .in_2(out_2[3]));
  ALU alu_1 (
    .FunSel(FUNSELALU), .ZCNO(alu_1_zcno), .out_6(out_1), .C_in(out_2[2]), .A(multiplexer_2_out),
    .B(multiplexer_3_out));
  PC__AR__SP pc_ar_sp_1 (
    .RegSel(ARFREGSEL), .FunSel(ARFFUNSEL), .out_6(pc_ar_sp_1_out_6), .out_7(pc_ar_sp_1_out_7),
    .in_1(multiplexer_4_out), .OutCSel(OUTCSEL), .OutDSel(OUTDSEL));
  Flag_Register flag_register_1 (.in_1(alu_1_zcno), .ZCNO(out_2));
  Clock CLOCK (.out(CLOCK_out));
  Multiplexer #(.width(8), .enable("false")) multiplexer_5 (
    .in0(out_1), .in1(pc_ar_sp_1_out_7), .out(multiplexer_5_out), .sel(MEMMUXSEL));
  RAM #(.bus("separate")) ram_1 (
    .addr(pc_ar_sp_1_out_6), .din(multiplexer_5_out), .data(ram_1_data), .str(MEMSTR), .sel(1'b1),
    .clk(CLOCK_out), .ld(MEMLD), .clr(1'b0));

  // Other names for the same wires on the sheet: Z = out_2[3]; IROUT[15:8] = out_3

  // Notes on the sheet:
  //   IR-REGISTER
  //   A
  //   RF
  //   B
  //   OutC
  //   OutD
  //   ARF
  //   OutFlagRegister
  //   MEMORY
endmodule

module Flag_Register (
  input  [3:0] in_1,
  output [3:0] ZCNO
);

  wire clock_1_out;

  Clock clock_1 (.out(clock_1_out));
  D_Flip_Flop d_ff_1 (.clk(clock_1_out), .D(in_1[3]), .Q(ZCNO[3]), .en(1'b1));  // open: Qn, preset, reset
  D_Flip_Flop d_ff_2 (.clk(clock_1_out), .D(in_1[2]), .Q(ZCNO[2]), .en(1'b1));  // open: Qn, preset, reset
  D_Flip_Flop d_ff_3 (.clk(clock_1_out), .D(in_1[1]), .Q(ZCNO[1]), .en(1'b1));  // open: Qn, preset, reset
  D_Flip_Flop d_ff_4 (.clk(clock_1_out), .D(in_1[0]), .Q(ZCNO[0]), .en(1'b1));  // open: Qn, preset, reset
endmodule

module PC__AR__SP (
  input  [7:0] in_1,
  input  [1:0] OutCSel,
  input  [2:0] RegSel,
  input  [1:0] FunSel,
  input  [1:0] OutDSel,
  output [7:0] out_6,
  output [7:0] out_7
);

  wire [7:0] n8_bit_register_1_out_5, n8_bit_register_2_out_5, n8_bit_register_3_out_5;

  _8_bit_register u_8_bit_register_1 (
    .out_5(n8_bit_register_1_out_5), .in_3(FunSel), .in_4(in_1), .in_2(RegSel[0]));  // open: in_1
  _8_bit_register u_8_bit_register_2 (
    .out_5(n8_bit_register_2_out_5), .in_3(FunSel), .in_4(in_1), .in_2(RegSel[1]));  // open: in_1
  _8_bit_register u_8_bit_register_3 (
    .out_5(n8_bit_register_3_out_5), .in_3(FunSel), .in_4(in_1), .in_2(RegSel[2]));  // open: in_1
  Multiplexer #(.select(2), .width(8)) multiplexer_1 (
    .in0(n8_bit_register_1_out_5), .in1(n8_bit_register_1_out_5), .in2(n8_bit_register_2_out_5),
    .in3(n8_bit_register_3_out_5), .out(out_6), .sel(OutCSel), .en(1'b1));
  Multiplexer #(.select(2), .width(8)) multiplexer_2 (
    .in0(n8_bit_register_1_out_5), .in1(n8_bit_register_1_out_5), .in2(n8_bit_register_2_out_5),
    .in3(n8_bit_register_3_out_5), .out(out_7), .sel(OutDSel), .en(1'b1));

  // Notes on the sheet:
  //   PC
  //   AR
  //   SP
endmodule

module Control_Unit (
  input  [15:0] in_1,
  input  in_2,
  output LD_M,
  output out_4,
  output IR_EN,
  output IRL_H,
  output MEMSTR,
  output out_8,
  output [3:0] FUNSELALU,
  output [1:0] out_10,
  output out_11,
  output [1:0] out_12,
  output [1:0] out_13,
  output [1:0] RFFUNSEL,
  output [1:0] out_15,
  output [1:0] OUTASEL,
  output [1:0] out_17,
  output [1:0] out_18,
  output [3:0] out_19,
  output [2:0] out_20,
  output [1:0] out_21
);

  wire and_1_out, and_2_out, and_3_out, and_4_out, and_5_out, and_6_out, and_7_out, and_8_out, and_9_out,
       and_10_out, and_11_out, and_12_out, and_13_out, and_14_out, and_15_out, and_16_out, and_17_out,
       and_19_out, and_20_out, and_21_out, and_22_out, and_23_out, and_24_out, and_25_out, and_26_out,
       and_27_out, and_28_out, and_29_out, and_30_out, and_31_out, and_32_out, and_33_out, and_34_out,
       and_36_out, and_37_out, and_38_out, and_40_out, and_41_out, and_42_out, and_43_out, and_44_out,
       and_45_out, and_46_out, and_47_out, and_48_out, and_53_out, and_54_out, and_55_out, and_56_out,
       and_57_out, and_58_out, and_59_out, and_60_out, and_61_out, and_62_out, and_63_out, and_64_out,
       and_65_out, and_66_out, and_67_out, and_68_out, and_69_out, and_70_out, and_71_out, and_72_out,
       CLEARSC, D0, D1, D2, D3, D4, D5, D6, D7, D8, D9, D10, D11, D12, D13, D14, D15, D16, D17, D18,
       decoder_3_out0, decoder_3_out1, decoder_3_out2, decoder_3_out3, not_1_out, not_2_out, not_3_out,
       not_4_out, not_5_out, not_6_out, not_7_out, not_8_out, or_1_out, or_2_out, or_3_out, or_4_out,
       or_5_out, or_6_out, or_7_out, or_8_out, or_9_out, or_10_out, or_11_out, or_12_out, or_13_out,
       or_14_out, or_15_out, or_17_out, or_18_out, or_19_out, or_20_out, or_21_out, or_22_out, or_23_out,
       or_24_out, or_25_out, or_26_out, or_27_out, or_28_out, or_29_out, or_30_out, or_31_out, or_32_out,
       or_33_out, or_34_out, or_35_out, or_36_out, or_37_out, or_38_out, or_39_out, or_40_out, or_42_out,
       or_43_out, or_45_out, or_46_out, or_47_out, or_48_out, or_49_out, or_50_out, or_51_out, or_53_out,
       or_54_out, or_55_out, or_56_out, or_57_out, or_58_out, or_59_out, or_60_out, T0, T2, T3;
  wire [1:0] and_39_out;
  wire [2:0] and_18_out, multiplexer_1_out;
  wire [3:0] and_52_out, decoder_2_out3;

  not not_1 (not_1_out, in_2);
  or or_1 (or_1_out, D4, D8, D18);
  and and_1 (and_1_out, or_1_out, T2);
  or or_2 (or_2_out, D3, D7, D17);
  and and_2 (and_2_out, not_1_out, D16);
  and and_3 (and_3_out, in_2, D15);
  or or_3 (or_3_out, D17, D18);
  Multiplexer #(.select(2), .width(3), .enable("false")) multiplexer_1 (
    .in0(3'b001), .in1(3'b001), .in2(3'b010), .in3(3'b100), .out(multiplexer_1_out), .sel(in_1[7:6]));
  and and_4 (and_4_out, T2, D7);
  and and_5 (and_5_out, T2, D8);
  and and_6 (and_6_out, T3, D4);
  or or_4 (or_4_out, and_1_out, T0, IRL_H);
  and and_7 (and_7_out, or_2_out, T2);
  or or_5 (or_5_out, D4, D17, D18);
  and and_8 (and_8_out, D16, not_2_out);
  not not_2 (not_2_out, in_2);
  or or_6 (or_6_out, D3, D4, D18, D17);
  or or_7 (or_7_out, and_2_out, D14, and_3_out);
  and and_9 (and_9_out, T3, or_3_out);
  Decoder #(.select(5), .enable("false")) decoder_1 (
    .out0(D0), .out1(D1), .out2(D2), .out3(D3), .out4(D4), .out5(D5), .out6(D6), .out7(D7), .out8(D8),
    .out9(D9), .out10(D10), .out11(D11), .out12(D12), .out13(D13), .out14(D14), .out15(D15), .out16(D16),
    .out17(D17), .out18(D18), .sel(in_1[15:11]));  // open: out19, out20, out21, out22, out23, out24, out25, out26, out27, out28, out29, out30, out31
  Multiplexer #(.select(4), .width(4), .enable("false")) multiplexer_2 (
    .in1(4'b0000), .in2(4'b0000), .in3(4'b0000), .in5(4'b0001), .in6(4'b0011), .in7(4'b0000), .in8(4'b0000),
    .in9(4'b0100), .in10(4'b0101), .in11(4'b0110), .in12(4'b1000), .in13(4'b1001), .out(FUNSELALU),
    .sel(in_1[14:11]));  // open: in0, in4, in14, in15
  or or_8 (or_8_out, D1, D5, D6, D9, D10, D11, D12, D13);
  and and_10 (and_10_out, D15, in_2);
  or or_9 (or_9_out, and_10_out, D14);
  and and_11 (and_11_out, T2, D18);
  Multiplexer #(.width(2)) multiplexer_3 (.in0(2'b01), .in1(2'b10), .out(RFFUNSEL), .sel(and_4_out), .en(or_10_out));
  or or_10 (or_10_out, and_4_out, and_5_out);
  Multiplexer #(.width(2)) multiplexer_4 (.in1(2'b11), .out(RFFUNSEL), .sel(or_11_out), .en(or_11_out));  // open: in0
  or or_11 (or_11_out, and_6_out, and_12_out);
  and and_12 (and_12_out, T2, or_12_out);
  or or_12 (or_12_out, D0, D2, D5, D6, D10, D13, D12, D11, D9);
  Multiplexer #(.width(2)) multiplexer_5 (.in0(2'b01), .in1(2'b10), .out(out_17), .sel(and_7_out), .en(or_13_out));
  or or_13 (or_13_out, or_4_out, and_7_out);
  Multiplexer #(.width(2)) multiplexer_6 (.in1(2'b11), .out(out_17), .sel(and_13_out), .en(or_14_out));  // open: in0
  or or_14 (or_14_out, and_14_out, and_13_out);
  and and_13 (and_13_out, T2, or_15_out);
  and and_14 (and_14_out, or_5_out, T3);
  or or_15 (or_15_out, and_8_out, D2, D5, D6, D9, D10, D11, D12, D13, D14, and_15_out);
  and and_15 (and_15_out, in_2, D15);
  and and_16 (and_16_out, or_6_out, T2);
  and and_17 (and_17_out, or_7_out, T2);
  assign and_18_out = multiplexer_1_out & {3{in_1[8]}};  // AND_Gate and_18, 3 bits wide
  and and_19 (and_19_out, D4, T3);
  or or_16 (IR_EN, T0, IRL_H);
  and and_20 (and_20_out, T3, D4);
  and and_21 (and_21_out, D0, in_1[8]);
  not not_3 (not_3_out, in_1[8]);
  and and_22 (and_22_out, D16, not_4_out);
  not not_4 (not_4_out, in_2);
  and and_23 (and_23_out, T3, D17);
  or or_17 (or_17_out, D5, D6, D9, D10, D11, D12, D13);
  and and_24 (and_24_out, or_9_out, T2);
  Multiplexer #(.width(3)) multiplexer_7 (.in0(3'b100), .in1(3'b001), .out(out_20), .sel(or_19_out), .en(or_18_out));
  or or_18 (or_18_out, and_16_out, or_19_out);
  or or_19 (or_19_out, T0, IRL_H, and_17_out, and_9_out);
  Multiplexer #(.width(3)) multiplexer_8 (
    .in1(and_18_out), .out(out_20), .sel(or_20_out), .en(or_20_out));  // open: in0
  or or_20 (or_20_out, and_19_out, and_25_out);
  and and_25 (and_25_out, T2, or_21_out);
  or or_21 (or_21_out, D2, D5, D6, D7, D8, D10, D11, D12, D13, D9);
  and and_26 (and_26_out, D15, in_2);
  or or_22 (or_22_out, and_20_out, and_21_out);
  and and_27 (and_27_out, T2, or_8_out);
  and and_28 (and_28_out, T2, D2);
  and and_29 (and_29_out, T2, not_3_out, D0);
  and and_30 (and_30_out, T3, D4);
  Sequence_Counter sequence_counter_1 (.CLEARSC(CLEARSC), .out_2(T0), .out_3(IRL_H), .out_4(T2), .out_5(T3));
  Multiplexer #(.width(2)) multiplexer_9 (.in0(2'b00), .in1(2'b10), .out(out_10), .sel(or_22_out), .en(or_23_out));
  or or_23 (or_23_out, or_22_out, and_27_out);
  Multiplexer #(.width(2)) multiplexer_10 (
    .in0(2'b11), .in1({in_1[8], in_1[5]}), .out(out_10), .sel(and_28_out), .en(or_24_out));
  or or_24 (or_24_out, and_28_out, and_29_out);
  or or_25 (or_25_out, and_22_out, and_23_out);
  and and_31 (and_31_out, T2, or_17_out);
  and and_32 (and_32_out, T2, D2);
  or or_26 (or_26_out, and_24_out, and_11_out, and_30_out);
  and and_33 (and_33_out, T3, D8);
  and and_34 (and_34_out, D0, T2, in_1[8]);
  or or_27 (or_27_out, and_26_out, D14, D18);
  or or_28 (or_28_out, D17, D4);
  Multiplexer #(.select(2), .enable("false")) multiplexer_11 (
    .in0(1'b0), .in1(in_1[5]), .in2(in_1[2]), .out(out_8), .sel(and_39_out));  // open: in3
  and and_35 (and_39_out[1], or_29_out, T2);
  or or_29 (or_29_out, D6, D5, D9, D10);
  Multiplexer #(.width(2)) multiplexer_12 (.in0(2'b00), .in1(2'b01), .out(out_13), .sel(or_25_out), .en(or_30_out));
  or or_30 (or_30_out, or_25_out, and_31_out);
  Multiplexer #(.width(2)) multiplexer_13 (
    .in0(2'b10), .in1({2{in_1[5]}}), .out(out_13), .sel(and_32_out), .en(or_31_out));
  or or_31 (or_31_out, and_32_out, or_26_out);
  and and_36 (and_36_out, T3, D7);
  or or_32 (or_32_out, D5, D6, D9, D10);
  or or_33 (or_33_out, D5, D6, D9, D10);
  Decoder #(.select(2), .enable("false")) decoder_2 (
    .out0(decoder_2_out3[3]), .out1(decoder_2_out3[2]), .out2(decoder_2_out3[1]), .out3(decoder_2_out3[0]),
    .sel(in_1[10:9]));
  Decoder #(.select(2), .enable("false")) decoder_3 (
    .out0(decoder_3_out0), .out1(decoder_3_out1), .out2(decoder_3_out2), .out3(decoder_3_out3),
    .sel(in_1[7:6]));
  and and_37 (and_37_out, T2, D18);
  and and_38 (and_38_out, T2, or_27_out);
  and and_39 (and_39_out[0], or_34_out, T2);
  or or_34 (or_34_out, D13, D12, D11);
  or or_35 (or_35_out, or_36_out, and_44_out);
  or or_36 (or_36_out, and_33_out, and_36_out);
  or or_37 (or_37_out, and_40_out, and_45_out);
  and and_40 (and_40_out, T2, or_32_out);
  and and_41 (and_41_out, T2, D17);
  or or_38 (or_38_out, and_42_out, and_46_out);
  and and_42 (and_42_out, T2, or_33_out);
  and and_43 (and_43_out, T3, or_28_out);
  Multiplexer #(.width(2)) multiplexer_14 (
    .in0(in_1[7:6]), .in1(in_1[10:9]), .out(OUTASEL), .sel(and_44_out), .en(or_35_out));
  and and_44 (and_44_out, T2, D1);
  Multiplexer #(.width(2)) multiplexer_15 (
    .in0(in_1[4:3]), .in1(in_1[1:0]), .out(OUTASEL), .sel(and_40_out), .en(or_37_out));
  and and_45 (and_45_out, T2, or_39_out);
  or or_39 (or_39_out, D2, D3, D11, D13, D12);
  Multiplexer #(.width(2)) multiplexer_16 (.in1(2'b00), .out(out_18), .sel(and_41_out), .en(and_41_out));  // open: in0
  Multiplexer #(.width(2)) multiplexer_17 (
    .in0(in_1[4:3]), .in1(in_1[1:0]), .out(out_18), .sel(and_42_out), .en(or_38_out));
  and and_46 (and_46_out, T2, or_40_out);
  or or_40 (or_40_out, D3, D11, D13, D12);
  not not_5 (not_5_out, in_1[8]);
  or or_41 (LD_M, and_34_out, and_37_out, T0, and_38_out, and_43_out, IRL_H);
  Multiplexer multiplexer_18 (.in0(in_1[5]), .in1(1'b1), .out(out_11), .sel(and_53_out), .en(or_42_out));
  or or_42 (or_42_out, and_47_out, and_53_out);
  and and_47 (and_47_out, T2, D3);
  Multiplexer multiplexer_19 (.in1(1'b0), .out(out_11), .sel(and_48_out), .en(and_48_out));  // open: in0
  and and_48 (and_48_out, T2, D1);
  and and_49 (and_52_out[3], not_5_out, decoder_3_out0);
  and and_50 (and_52_out[2], decoder_3_out1, not_5_out);
  and and_51 (and_52_out[1], not_5_out, decoder_3_out2);
  and and_52 (and_52_out[0], not_5_out, decoder_3_out3);
  not not_6 (not_6_out, in_1[8]);
  or or_43 (or_43_out, D3, D17);
  and and_53 (and_53_out, D17, T2);
  and and_54 (and_54_out, D0, not_6_out);
  and and_55 (and_55_out, D0, in_1[8]);
  and and_56 (and_56_out, D14, D15, not_6_out);
  and and_57 (and_57_out, in_1[8], D16, in_2);
  not not_7 (not_7_out, in_2);
  and and_58 (and_58_out, not_7_out, D17, in_1[8]);
  and and_59 (and_59_out, or_43_out, T2);
  and and_60 (and_60_out, D1, T2);
  and and_61 (and_61_out, T2, or_45_out);
  or or_44 (MEMSTR, and_59_out, and_60_out);
  Multiplexer #(.width(2)) multiplexer_20 (
    .in1(in_1[4:3]), .out(out_12), .sel(and_61_out), .en(and_61_out));  // open: in0
  or or_45 (or_45_out, D5, D6, D9, D10);
  or or_46 (or_46_out, and_58_out, D18, D4, D4, D8, D7, D7);
  Multiplexer #(.width(4)) multiplexer_21 (
    .in0(decoder_2_out3), .in1(and_52_out), .out(out_19), .sel(or_57_out), .en(or_47_out));
  or or_47 (or_47_out, or_48_out, or_57_out);
  or or_48 (or_48_out, and_62_out, and_66_out);
  and and_62 (and_62_out, T2, D0, not_8_out);
  not not_8 (not_8_out, in_1[8]);
  or or_49 (or_49_out, and_54_out, D10, D9, D12, D13, D11, and_56_out, and_57_out, and_55_out, D3, D1, D5, D6, D1, D2);
  and and_63 (and_63_out, T2, or_49_out);
  and and_64 (and_64_out, T3, or_46_out);
  and and_65 (and_65_out, D0, in_1[8]);
  or or_50 (or_50_out, D17, D3);
  or or_51 (or_51_out, D18, D4);
  and and_66 (and_66_out, T2, D0, in_1[8]);
  and and_67 (and_67_out, or_50_out, T2);
  and and_68 (and_68_out, T3, or_51_out);
  or or_52 (CLEARSC, and_63_out, and_64_out);
  or or_53 (or_53_out, T0, IRL_H);
  or or_54 (or_54_out, D1, and_65_out);
  or or_55 (or_55_out, D10, D9, D6, D5, D2);
  and and_69 (and_69_out, T2, or_58_out);
  and and_70 (and_70_out, T2, or_54_out);
  or or_56 (or_56_out, and_67_out, and_68_out);
  and and_71 (and_71_out, or_55_out, T2);
  or or_57 (or_57_out, and_69_out, and_72_out);
  or or_58 (or_58_out, D2, D5, D6, D7, D8, D10, D11, D12, D13, D9);
  Multiplexer #(.width(2)) multiplexer_22 (.in0(2'b00), .in1(2'b10), .out(out_15), .sel(and_70_out), .en(or_59_out));
  or or_59 (or_59_out, or_53_out, and_70_out);
  Multiplexer #(.width(2)) multiplexer_23 (
    .in0(2'b11), .in1(in_1[4:3]), .out(out_15), .sel(and_71_out), .en(or_60_out));
  or or_60 (or_60_out, or_56_out, and_71_out);
  and and_72 (and_72_out, T3, D4);

  assign out_4 = in_1[5];
  assign out_21 = 2'b11;

  // Other names for the same wires on the sheet: IR11 = in_1[11]; IROUT[15:0] = in_1; IR12 = in_1[12];
  //   IR13 = in_1[13]; IR14 = in_1[14]; IR8 = in_1[8]; BSELALU = in_1[5]; IR5 = in_1[5]; IR0 = in_1[0]; IR1 = in_1[1];
  //   IR9 = in_1[9]; IR10 = in_1[10]; IR6 = in_1[6]; IR7 = in_1[7]; IR3 = in_1[3]; IR4 = in_1[4];
  //   AMUXSEL[1:0] = out_10; ARFFUNSEL[1:0] = out_17; ARFREGSEL[2:0] = out_20; ASELALU = out_8; BMUXSEL[1:0] = out_13;
  //   IR2 = in_1[2]; IR15 = in_1[15]; MEMLD = LD_M; MEMMUXSEL = out_11; OUTBSEL[1:0] = out_12; OUTCSEL[1:0] = out_15;
  //   OUTDSEL[1:0] = out_18; RFREGSEL[3:0] = out_19; IRL_H_prime = IRL_H; T1 = IRL_H; Z = in_2
endmodule

module Sequence_Counter (
  input  CLEARSC,
  output out_2,
  output out_3,
  output out_4,
  output out_5
);

  wire CLOCK;
  wire [1:0] adder_1_out, multiplexer_1_out, register_1_q;

  Adder #(.width(2)) adder_1 (.a(register_1_q), .b(2'b01), .out(adder_1_out));  // open: cin, cout
  Multiplexer #(.width(2), .enable("false")) multiplexer_1 (
    .in0(adder_1_out), .in1(2'b00), .out(multiplexer_1_out), .sel(CLEARSC));
  Register #(.width(2)) register_1 (.D(multiplexer_1_out), .Q(register_1_q), .clk(CLOCK));  // open: en, clr
  Clock clock_1 (.out(CLOCK));
  Decoder #(.select(2), .enable("false")) decoder_1 (
    .out0(out_2), .out1(out_3), .out2(out_4), .out3(out_5), .sel(register_1_q));
endmodule
