// Logisim project total.circ as structural Verilog: 11 circuits, main circuit main
module main (
  input  in_1,
  input  in_2,
  input  s1,
  input  in_4,
  input  in_5,
  input  I1,
  input  I2,
  input  I3,
  input  I4,
  input  I5,
  input  I6,
  input  I7,
  output Q0,
  output Q1,
  output Q2,
  output Q3,
  output Q4,
  output Q5,
  output Q6,
  output Q7
);

  wire clock_1_out, n4_1_mux_1_out_7, n4_1_mux_2_out_7, n4_1_mux_3_out_7, n4_1_mux_4_out_7, n4_1_mux_5_out_7,
       n4_1_mux_6_out_7, n4_1_mux_7_out_7, n4_1_mux_8_out_7, n8_input_register_decrement_1_out_9,
       n8_input_register_decrement_1_out_10, n8_input_register_decrement_1_out_11,
       n8_input_register_decrement_1_out_12, n8_input_register_decrement_1_out_13,
       n8_input_register_decrement_1_out_14, n8_input_register_decrement_1_out_15,
       n8_input_register_increment_1_out_9, n8_input_register_increment_1_out_10,
       n8_input_register_increment_1_out_11, n8_input_register_increment_1_out_12,
       n8_input_register_increment_1_out_13, n8_input_register_increment_1_out_14,
       n8_input_register_increment_1_out_15, n8_input_register_increment_1_out_16;

  _8_input_register_increment u_8_input_register_increment_1 (
    .out_9(n8_input_register_increment_1_out_9), .out_11(n8_input_register_increment_1_out_11),
    .out_12(n8_input_register_increment_1_out_12), .out_13(n8_input_register_increment_1_out_13),
    .out_14(n8_input_register_increment_1_out_14), .out_15(n8_input_register_increment_1_out_15),
    .out_16(n8_input_register_increment_1_out_16), .out_10(n8_input_register_increment_1_out_10), .in_1(Q0),
    .in_2(Q1), .in_3(Q2), .in_4(Q3), .in_5(Q4), .in_6(Q5), .in_7(Q6), .in_8(Q7));
  _8_input___register_decrement u_8_input_register_decrement_1 (
    .in_1(Q0), .in_2(Q1), .in_3(Q2), .in_4(Q3), .in_5(Q4), .in_6(Q5), .in_7(Q6), .in_8(Q7),
    .out_9(n8_input_register_decrement_1_out_9), .out_10(n8_input_register_decrement_1_out_10),
    .out_11(n8_input_register_decrement_1_out_11), .out_12(n8_input_register_decrement_1_out_12),
    .out_13(n8_input_register_decrement_1_out_13), .out_14(n8_input_register_decrement_1_out_14),
    .out_15(n8_input_register_decrement_1_out_15));
  _4_1_MUX u_4_1_mux_1 (
    .s0(in_4), .s1(s1), .out_7(n4_1_mux_1_out_7), .in_1(in_1), .in_2(n8_input_register_increment_1_out_9),
    .in_3(n8_input_register_increment_1_out_9), .in_4(in_5));
  _4_1_MUX u_4_1_mux_2 (
    .s0(in_4), .s1(s1), .out_7(n4_1_mux_2_out_7), .in_1(in_1), .in_2(n8_input_register_increment_1_out_11),
    .in_3(n8_input_register_decrement_1_out_9), .in_4(I1));
  _4_1_MUX u_4_1_mux_3 (
    .s0(in_4), .s1(s1), .out_7(n4_1_mux_3_out_7), .in_1(in_1), .in_2(n8_input_register_increment_1_out_10),
    .in_3(n8_input_register_decrement_1_out_10), .in_4(I2));
  _4_1_MUX u_4_1_mux_4 (
    .s0(in_4), .s1(s1), .out_7(n4_1_mux_4_out_7), .in_1(in_1), .in_2(n8_input_register_increment_1_out_12),
    .in_3(n8_input_register_decrement_1_out_11), .in_4(I3));
  _4_1_MUX u_4_1_mux_5 (
    .s0(in_4), .s1(s1), .out_7(n4_1_mux_5_out_7), .in_1(in_1), .in_2(n8_input_register_increment_1_out_13),
    .in_3(n8_input_register_decrement_1_out_12), .in_4(I4));
  _4_1_MUX u_4_1_mux_6 (
    .s0(in_4), .s1(s1), .out_7(n4_1_mux_6_out_7), .in_1(in_1), .in_2(n8_input_register_increment_1_out_14),
    .in_3(n8_input_register_decrement_1_out_13), .in_4(I5));
  _4_1_MUX u_4_1_mux_7 (
    .s0(in_4), .s1(s1), .out_7(n4_1_mux_7_out_7), .in_1(in_1), .in_2(n8_input_register_increment_1_out_15),
    .in_3(n8_input_register_decrement_1_out_14), .in_4(I6));
  _4_1_MUX u_4_1_mux_8 (
    .s0(in_4), .s1(s1), .out_7(n4_1_mux_8_out_7), .in_1(in_1), .in_2(n8_input_register_increment_1_out_16),
    .in_3(n8_input_register_decrement_1_out_15), .in_4(I7));
  Clock clock_1 (.out(clock_1_out));
  D_Flip_Flop d_ff_1 (.clk(clock_1_out), .D(n4_1_mux_1_out_7), .Q(Q0), .en(in_2));  // open: Qn, preset, reset
  D_Flip_Flop d_ff_2 (.clk(clock_1_out), .D(n4_1_mux_2_out_7), .Q(Q1), .en(in_2));  // open: Qn, preset, reset
  D_Flip_Flop d_ff_3 (.clk(clock_1_out), .D(n4_1_mux_3_out_7), .Q(Q2), .en(in_2));  // open: Qn, preset, reset
  D_Flip_Flop d_ff_4 (.clk(clock_1_out), .D(n4_1_mux_4_out_7), .Q(Q3), .en(in_2));  // open: Qn, preset, reset
  D_Flip_Flop d_ff_5 (.clk(clock_1_out), .D(n4_1_mux_5_out_7), .Q(Q4), .en(in_2));  // open: Qn, preset, reset
  D_Flip_Flop d_ff_6 (.clk(clock_1_out), .D(n4_1_mux_6_out_7), .Q(Q5), .en(in_2));  // open: Qn, preset, reset
  D_Flip_Flop d_ff_7 (.clk(clock_1_out), .D(n4_1_mux_7_out_7), .Q(Q6), .en(in_2));  // open: Qn, preset, reset
  D_Flip_Flop d_ff_8 (.clk(clock_1_out), .D(n4_1_mux_8_out_7), .Q(Q7), .en(in_2));  // open: Qn, preset, reset
  // also tied to VCC on the sheet: in_2

  // Notes on the sheet:
  //   I0
  //   Register Increment
  //   Register Decrement
  //   s0
endmodule

module _4_1_MUX (
  input  in_1,
  input  in_2,
  input  in_3,
  input  in_4,
  input  s0,
  input  s1,
  output out_7
);

  wire multiplexer_1_out, multiplexer_2_out;

  Multiplexer #(.enable("false")) multiplexer_1 (.in0(in_1), .in1(in_2), .out(multiplexer_1_out), .sel(s1));
  Multiplexer #(.enable("false")) multiplexer_2 (.in0(in_3), .in1(in_4), .out(multiplexer_2_out), .sel(s1));
  Multiplexer #(.enable("false")) multiplexer_3 (
    .in0(multiplexer_1_out), .in1(multiplexer_2_out), .out(out_7), .sel(s0));
endmodule

module _8_input_register_increment (
  input  in_1,
  input  in_2,
  input  in_3,
  input  in_4,
  input  in_5,
  input  in_6,
  input  in_7,
  input  in_8,
  output out_9,
  output out_10,
  output out_11,
  output out_12,
  output out_13,
  output out_14,
  output out_15,
  output out_16
);

  wire and_1_out, and_2_out, and_3_out, and_4_out, and_5_out, and_6_out;

  not not_1 (out_9, in_1);
  and and_1 (and_1_out, in_1, in_2);
  xor xor_1 (out_11, in_1, in_2);
  and and_2 (and_2_out, and_1_out, in_3);
  xor xor_2 (out_10, and_1_out, in_3);
  and and_3 (and_3_out, and_2_out, in_4);
  and and_4 (and_4_out, and_3_out, in_5);
  xor xor_3 (out_12, and_2_out, in_4);
  xor xor_4 (out_13, and_3_out, in_5);
  and and_5 (and_5_out, and_4_out, in_6);
  and and_6 (and_6_out, and_5_out, in_7);
  xor xor_5 (out_14, and_4_out, in_6);
  xor xor_6 (out_15, and_5_out, in_7);
  xor xor_7 (out_16, and_6_out, in_8);
endmodule

module _8_input___register_decrement (
  input  in_1,
  input  in_2,
  input  in_3,
  input  in_4,
  input  in_5,
  input  in_6,
  input  in_7,
  input  in_8,
  output out_9,
  output out_10,
  output out_11,
  output out_12,
  output out_13,
  output out_14,
  output out_15
);

  wire or_1_out, or_2_out, or_3_out, or_4_out, or_5_out, or_6_out;

  or or_1 (or_1_out, in_1, in_2);
  xnor xnor_1 (out_9, in_1, in_2);
  or or_2 (or_2_out, or_1_out, in_3);
  xnor xnor_2 (out_10, or_1_out, in_3);
  or or_3 (or_3_out, or_2_out, in_4);
  xnor xnor_3 (out_11, or_2_out, in_4);
  or or_4 (or_4_out, or_3_out, in_5);
  xnor xnor_4 (out_12, or_3_out, in_5);
  or or_5 (or_5_out, or_4_out, in_6);
  or or_6 (or_6_out, or_5_out, in_7);
  xnor xnor_5 (out_13, or_4_out, in_6);
  xnor xnor_6 (out_14, or_5_out, in_7);
  xnor xnor_7 (out_15, or_6_out, in_8);
endmodule

module _8_bit_register (
  input  in_1,
  input  in_2,
  input  [1:0] in_3,
  input  [7:0] in_4,
  output [7:0] out_5
);

  wire clock_1_out, multiplexer_1_out, multiplexer_2_out, multiplexer_3_out, multiplexer_4_out,
       multiplexer_5_out, multiplexer_6_out, multiplexer_7_out, multiplexer_8_out,
       n8_input_register_decrement_1_out_9, n8_input_register_decrement_1_out_10,
       n8_input_register_decrement_1_out_11, n8_input_register_decrement_1_out_12,
       n8_input_register_decrement_1_out_13, n8_input_register_decrement_1_out_14,
       n8_input_register_decrement_1_out_15, n8_input_register_increment_1_out_9,
       n8_input_register_increment_1_out_10, n8_input_register_increment_1_out_11,
       n8_input_register_increment_1_out_12, n8_input_register_increment_1_out_13,
       n8_input_register_increment_1_out_14, n8_input_register_increment_1_out_15,
       n8_input_register_increment_1_out_16;

  _8_input_register_increment u_8_input_register_increment_1 (
    .out_9(n8_input_register_increment_1_out_9), .out_11(n8_input_register_increment_1_out_11),
    .out_12(n8_input_register_increment_1_out_12), .out_13(n8_input_register_increment_1_out_13),
    .out_14(n8_input_register_increment_1_out_14), .out_15(n8_input_register_increment_1_out_15),
    .out_16(n8_input_register_increment_1_out_16), .out_10(n8_input_register_increment_1_out_10),
    .in_1(out_5[0]), .in_2(out_5[1]), .in_3(out_5[2]), .in_4(out_5[3]), .in_5(out_5[4]), .in_6(out_5[5]),
    .in_7(out_5[6]), .in_8(out_5[7]));
  _8_input___register_decrement u_8_input_register_decrement_1 (
    .in_1(out_5[0]), .in_2(out_5[1]), .in_3(out_5[2]), .in_4(out_5[3]), .in_5(out_5[4]), .in_6(out_5[5]),
    .in_7(out_5[6]), .in_8(out_5[7]), .out_9(n8_input_register_decrement_1_out_9),
    .out_10(n8_input_register_decrement_1_out_10), .out_11(n8_input_register_decrement_1_out_11),
    .out_12(n8_input_register_decrement_1_out_12), .out_13(n8_input_register_decrement_1_out_13),
    .out_14(n8_input_register_decrement_1_out_14), .out_15(n8_input_register_decrement_1_out_15));
  Multiplexer #(.select(2)) multiplexer_1 (
    .in0(in_1), .in1(n8_input_register_increment_1_out_9), .in2(n8_input_register_increment_1_out_9),
    .in3(in_4[0]), .out(multiplexer_1_out), .sel(in_3), .en(in_2));
  Multiplexer #(.select(2)) multiplexer_2 (
    .in0(in_1), .in1(n8_input_register_increment_1_out_11), .in2(n8_input_register_decrement_1_out_9),
    .in3(in_4[1]), .out(multiplexer_2_out), .sel(in_3), .en(in_2));
  Multiplexer #(.select(2)) multiplexer_3 (
    .in0(in_1), .in1(n8_input_register_increment_1_out_10), .in2(n8_input_register_decrement_1_out_10),
    .in3(in_4[2]), .out(multiplexer_3_out), .sel(in_3), .en(in_2));
  Multiplexer #(.select(2)) multiplexer_4 (
    .in0(in_1), .in1(n8_input_register_increment_1_out_12), .in2(n8_input_register_decrement_1_out_11),
    .in3(in_4[3]), .out(multiplexer_4_out), .sel(in_3), .en(in_2));
  Multiplexer #(.select(2)) multiplexer_5 (
    .in0(in_1), .in1(n8_input_register_increment_1_out_13), .in2(n8_input_register_decrement_1_out_12),
    .in3(in_4[4]), .out(multiplexer_5_out), .sel(in_3), .en(in_2));
  Multiplexer #(.select(2)) multiplexer_6 (
    .in0(in_1), .in1(n8_input_register_increment_1_out_14), .in2(n8_input_register_decrement_1_out_13),
    .in3(in_4[5]), .out(multiplexer_6_out), .sel(in_3), .en(in_2));
  Multiplexer #(.select(2)) multiplexer_7 (
    .in0(in_1), .in1(n8_input_register_increment_1_out_15), .in2(n8_input_register_decrement_1_out_14),
    .in3(in_4[6]), .out(multiplexer_7_out), .sel(in_3), .en(in_2));
  Multiplexer #(.select(2)) multiplexer_8 (
    .in0(in_1), .in1(n8_input_register_increment_1_out_16), .in2(n8_input_register_decrement_1_out_15),
    .in3(in_4[7]), .out(multiplexer_8_out), .sel(in_3), .en(in_2));
  Clock clock_1 (.out(clock_1_out));
  D_Flip_Flop d_ff_1 (.clk(clock_1_out), .D(multiplexer_1_out), .Q(out_5[0]), .en(in_2));  // open: Qn, preset, reset
  D_Flip_Flop d_ff_2 (.clk(clock_1_out), .D(multiplexer_2_out), .Q(out_5[1]), .en(in_2));  // open: Qn, preset, reset
  D_Flip_Flop d_ff_3 (.clk(clock_1_out), .D(multiplexer_3_out), .Q(out_5[2]), .en(in_2));  // open: Qn, preset, reset
  D_Flip_Flop d_ff_4 (.clk(clock_1_out), .D(multiplexer_4_out), .Q(out_5[3]), .en(in_2));  // open: Qn, preset, reset
  D_Flip_Flop d_ff_5 (.clk(clock_1_out), .D(multiplexer_5_out), .Q(out_5[4]), .en(in_2));  // open: Qn, preset, reset
  D_Flip_Flop d_ff_6 (.clk(clock_1_out), .D(multiplexer_6_out), .Q(out_5[5]), .en(in_2));  // open: Qn, preset, reset
  D_Flip_Flop d_ff_7 (.clk(clock_1_out), .D(multiplexer_7_out), .Q(out_5[6]), .en(in_2));  // open: Qn, preset, reset
  D_Flip_Flop d_ff_8 (.clk(clock_1_out), .D(multiplexer_8_out), .Q(out_5[7]), .en(in_2));  // open: Qn, preset, reset

  // Notes on the sheet:
  //   Register Increment
  //   Register Decrement
endmodule

module _16_input_register_increment (
  input  in_1,
  input  in_2,
  input  in_3,
  input  in_4,
  input  in_5,
  input  in_6,
  input  in_7,
  input  in_8,
  input  in_9,
  input  in_10,
  input  in_11,
  input  in_12,
  input  in_13,
  input  in_14,
  input  in_15,
  input  in_16,
  output out_17,
  output out_18,
  output out_19,
  output out_20,
  output out_21,
  output out_22,
  output out_23,
  output out_24,
  output out_25,
  output out_26,
  output out_27,
  output out_28,
  output out_29,
  output out_30,
  output out_31,
  output out_32
);

  wire and_1_out, and_2_out, and_3_out, and_4_out, and_5_out, and_6_out, and_7_out, and_8_out, and_9_out,
       and_10_out, and_11_out, and_12_out, and_13_out, and_14_out;

  not not_1 (out_17, in_1);
  and and_1 (and_1_out, in_1, in_2);
  xor xor_1 (out_19, in_1, in_2);
  and and_2 (and_2_out, and_1_out, in_3);
  xor xor_2 (out_18, and_1_out, in_3);
  and and_3 (and_3_out, and_2_out, in_4);
  and and_4 (and_4_out, and_3_out, in_5);
  xor xor_3 (out_20, and_2_out, in_4);
  xor xor_4 (out_21, and_3_out, in_5);
  and and_5 (and_5_out, and_4_out, in_6);
  and and_6 (and_6_out, and_5_out, in_7);
  and and_7 (and_7_out, and_6_out, in_8);
  and and_8 (and_8_out, and_11_out, in_10);
  and and_9 (and_9_out, and_12_out, in_12);
  and and_10 (and_10_out, and_13_out, in_14);
  xor xor_5 (out_22, and_4_out, in_6);
  xor xor_6 (out_23, and_5_out, in_7);
  xor xor_7 (out_25, and_7_out, in_9);
  and and_11 (and_11_out, and_7_out, in_9);
  and and_12 (and_12_out, and_8_out, in_11);
  xor xor_8 (out_24, and_6_out, in_8);
  xor xor_9 (out_27, and_8_out, in_11);
  xor xor_10 (out_29, and_9_out, in_13);
  and and_13 (and_13_out, and_9_out, in_13);
  xor xor_11 (out_31, and_10_out, in_15);
  and and_14 (and_14_out, and_10_out, in_15);
  xor xor_12 (out_26, and_11_out, in_10);
  xor xor_13 (out_28, and_12_out, in_12);
  xor xor_14 (out_30, and_13_out, in_14);
  xor xor_15 (out_32, and_14_out, in_16);
endmodule

module _16_input__register_decrement (
  input  in_1,
  input  in_2,
  input  in_3,
  input  in_4,
  input  in_5,
  input  in_6,
  input  in_7,
  input  in_8,
  input  in_9,
  input  in_10,
  input  in_11,
  input  in_12,
  input  in_13,
  input  in_14,
  input  in_15,
  input  in_16,
  output out_17,
  output out_18,
  output out_19,
  output out_20,
  output out_21,
  output out_22,
  output out_23,
  output out_24,
  output out_25,
  output out_26,
  output out_27,
  output out_28,
  output out_29,
  output out_30,
  output out_31
);

  wire or_1_out, or_2_out, or_3_out, or_4_out, or_5_out, or_6_out, or_7_out, or_8_out, or_9_out, or_10_out,
       or_11_out, or_12_out, or_13_out, or_14_out;

  or or_1 (or_1_out, in_1, in_2);
  or or_2 (or_2_out, or_1_out, in_3);
  xnor xnor_1 (out_17, or_1_out, in_3);
  or or_3 (or_3_out, or_2_out, in_4);
  xnor xnor_2 (out_18, in_1, in_2);
  or or_4 (or_4_out, or_3_out, in_5);
  or or_5 (or_5_out, or_4_out, in_6);
  xnor xnor_3 (out_19, or_2_out, in_4);
  xnor xnor_4 (out_20, or_3_out, in_5);
  or or_6 (or_6_out, or_5_out, in_7);
  or or_7 (or_7_out, or_6_out, in_8);
  or or_8 (or_8_out, or_11_out, in_10);
  or or_9 (or_9_out, or_12_out, in_12);
  or or_10 (or_10_out, or_13_out, in_14);
  xnor xnor_5 (out_21, or_4_out, in_6);
  xnor xnor_6 (out_22, or_5_out, in_7);
  or or_11 (or_11_out, or_7_out, in_9);
  or or_12 (or_12_out, or_8_out, in_11);
  xnor xnor_7 (out_23, or_6_out, in_8);
  xnor xnor_8 (out_24, or_7_out, in_9);
  xnor xnor_9 (out_26, or_8_out, in_11);
  xnor xnor_10 (out_28, or_9_out, in_13);
  or or_13 (or_13_out, or_9_out, in_13);
  or or_14 (or_14_out, or_10_out, in_15);
  xnor xnor_11 (out_25, or_11_out, in_10);
  xnor xnor_12 (out_27, or_12_out, in_12);
  xnor xnor_13 (out_29, or_13_out, in_14);
  xnor xnor_14 (out_30, or_10_out, in_15);
  xnor xnor_15 (out_31, or_14_out, in_16);
endmodule

module _16_bit__register (
  input  [1:0] in_1,
  input  in_2,
  input  [15:0] in_3,
  output [15:0] out_4
);

  wire clock_1_out, multiplexer_1_out, multiplexer_2_out, multiplexer_3_out, multiplexer_4_out,
       multiplexer_5_out, multiplexer_6_out, multiplexer_7_out, multiplexer_8_out, multiplexer_9_out,
       multiplexer_10_out, multiplexer_11_out, multiplexer_12_out, multiplexer_13_out, multiplexer_14_out,
       multiplexer_15_out, multiplexer_16_out, n16_input_register_decrement_1_out_17,
       n16_input_register_decrement_1_out_18, n16_input_register_decrement_1_out_19,
       n16_input_register_decrement_1_out_20, n16_input_register_decrement_1_out_21,
       n16_input_register_decrement_1_out_22, n16_input_register_decrement_1_out_23,
       n16_input_register_decrement_1_out_24, n16_input_register_decrement_1_out_25,
       n16_input_register_decrement_1_out_26, n16_input_register_decrement_1_out_27,
       n16_input_register_decrement_1_out_28, n16_input_register_decrement_1_out_29,
       n16_input_register_decrement_1_out_30, n16_input_register_decrement_1_out_31,
       n16_input_register_increment_1_out_17, n16_input_register_increment_1_out_18,
       n16_input_register_increment_1_out_19, n16_input_register_increment_1_out_20,
       n16_input_register_increment_1_out_21, n16_input_register_increment_1_out_22,
       n16_input_register_increment_1_out_23, n16_input_register_increment_1_out_24,
       n16_input_register_increment_1_out_25, n16_input_register_increment_1_out_26,
       n16_input_register_increment_1_out_27, n16_input_register_increment_1_out_28,
       n16_input_register_increment_1_out_29, n16_input_register_increment_1_out_30,
       n16_input_register_increment_1_out_31, n16_input_register_increment_1_out_32;

  _16_input_register_increment u_16_input_register_increment_1 (
    .in_1(out_4[0]), .in_2(out_4[1]), .in_3(out_4[2]), .in_4(out_4[3]), .in_5(out_4[4]), .in_6(out_4[5]),
    .in_7(out_4[6]), .in_8(out_4[7]), .in_9(out_4[8]), .in_10(out_4[9]), .in_11(out_4[10]),
    .in_12(out_4[11]), .in_13(out_4[12]), .in_14(out_4[13]), .in_15(out_4[14]), .in_16(out_4[15]),
    .out_17(n16_input_register_increment_1_out_17), .out_18(n16_input_register_increment_1_out_18),
    .out_19(n16_input_register_increment_1_out_19), .out_20(n16_input_register_increment_1_out_20),
    .out_21(n16_input_register_increment_1_out_21), .out_22(n16_input_register_increment_1_out_22),
    .out_23(n16_input_register_increment_1_out_23), .out_24(n16_input_register_increment_1_out_24),
    .out_25(n16_input_register_increment_1_out_25), .out_26(n16_input_register_increment_1_out_26),
    .out_27(n16_input_register_increment_1_out_27), .out_28(n16_input_register_increment_1_out_28),
    .out_29(n16_input_register_increment_1_out_29), .out_30(n16_input_register_increment_1_out_30),
    .out_31(n16_input_register_increment_1_out_31), .out_32(n16_input_register_increment_1_out_32));
  _16_input__register_decrement u_16_input_register_decrement_1 (
    .in_1(out_4[0]), .in_2(out_4[1]), .in_3(out_4[2]), .in_4(out_4[3]), .in_5(out_4[4]), .in_6(out_4[5]),
    .in_7(out_4[6]), .in_8(out_4[7]), .in_9(out_4[8]), .in_10(out_4[9]), .in_11(out_4[10]),
    .in_12(out_4[11]), .in_13(out_4[12]), .in_14(out_4[13]), .in_15(out_4[14]), .in_16(out_4[15]),
    .out_17(n16_input_register_decrement_1_out_17), .out_18(n16_input_register_decrement_1_out_18),
    .out_19(n16_input_register_decrement_1_out_19), .out_20(n16_input_register_decrement_1_out_20),
    .out_21(n16_input_register_decrement_1_out_21), .out_22(n16_input_register_decrement_1_out_22),
    .out_23(n16_input_register_decrement_1_out_23), .out_24(n16_input_register_decrement_1_out_24),
    .out_25(n16_input_register_decrement_1_out_25), .out_26(n16_input_register_decrement_1_out_26),
    .out_27(n16_input_register_decrement_1_out_27), .out_28(n16_input_register_decrement_1_out_28),
    .out_29(n16_input_register_decrement_1_out_29), .out_30(n16_input_register_decrement_1_out_30),
    .out_31(n16_input_register_decrement_1_out_31));
  Multiplexer #(.select(2)) multiplexer_1 (
    .in0(1'b0), .in1(n16_input_register_increment_1_out_17), .in2(n16_input_register_increment_1_out_17),
    .in3(in_3[0]), .out(multiplexer_1_out), .sel(in_1), .en(in_2));
  Multiplexer #(.select(2)) multiplexer_2 (
    .in0(1'b0), .in1(n16_input_register_increment_1_out_19), .in2(n16_input_register_decrement_1_out_18),
    .in3(in_3[1]), .out(multiplexer_2_out), .sel(in_1), .en(in_2));
  Multiplexer #(.select(2)) multiplexer_3 (
    .in0(1'b0), .in1(n16_input_register_increment_1_out_18), .in2(n16_input_register_decrement_1_out_17),
    .in3(in_3[2]), .out(multiplexer_3_out), .sel(in_1), .en(in_2));
  Multiplexer #(.select(2)) multiplexer_4 (
    .in0(1'b0), .in1(n16_input_register_increment_1_out_20), .in2(n16_input_register_decrement_1_out_19),
    .in3(in_3[3]), .out(multiplexer_4_out), .sel(in_1), .en(in_2));
  Multiplexer #(.select(2)) multiplexer_5 (
    .in0(1'b0), .in1(n16_input_register_increment_1_out_21), .in2(n16_input_register_decrement_1_out_20),
    .in3(in_3[4]), .out(multiplexer_5_out), .sel(in_1), .en(in_2));
  Multiplexer #(.select(2)) multiplexer_6 (
    .in0(1'b0), .in1(n16_input_register_increment_1_out_22), .in2(n16_input_register_decrement_1_out_21),
    .in3(in_3[5]), .out(multiplexer_6_out), .sel(in_1), .en(in_2));
  Multiplexer #(.select(2)) multiplexer_7 (
    .in0(1'b0), .in1(n16_input_register_increment_1_out_23), .in2(n16_input_register_decrement_1_out_22),
    .in3(in_3[6]), .out(multiplexer_7_out), .sel(in_1), .en(in_2));
  Multiplexer #(.select(2)) multiplexer_8 (
    .in0(1'b0), .in1(n16_input_register_increment_1_out_24), .in2(n16_input_register_decrement_1_out_23),
    .in3(in_3[7]), .out(multiplexer_8_out), .sel(in_1), .en(in_2));
  Multiplexer #(.select(2)) multiplexer_9 (
    .in0(1'b0), .in1(n16_input_register_increment_1_out_25), .in2(n16_input_register_decrement_1_out_24),
    .in3(in_3[8]), .out(multiplexer_9_out), .sel(in_1), .en(in_2));
  Multiplexer #(.select(2)) multiplexer_10 (
    .in0(1'b0), .in1(n16_input_register_increment_1_out_26), .in2(n16_input_register_decrement_1_out_25),
    .in3(in_3[9]), .out(multiplexer_10_out), .sel(in_1), .en(in_2));
  Multiplexer #(.select(2)) multiplexer_11 (
    .in0(1'b0), .in1(n16_input_register_increment_1_out_27), .in2(n16_input_register_decrement_1_out_26),
    .in3(in_3[10]), .out(multiplexer_11_out), .sel(in_1), .en(in_2));
  Multiplexer #(.select(2)) multiplexer_12 (
    .in0(1'b0), .in1(n16_input_register_increment_1_out_28), .in2(n16_input_register_decrement_1_out_27),
    .in3(in_3[11]), .out(multiplexer_12_out), .sel(in_1), .en(in_2));
  Multiplexer #(.select(2)) multiplexer_13 (
    .in0(1'b0), .in1(n16_input_register_increment_1_out_29), .in2(n16_input_register_decrement_1_out_28),
    .in3(in_3[12]), .out(multiplexer_13_out), .sel(in_1), .en(in_2));
  Multiplexer #(.select(2)) multiplexer_14 (
    .in0(1'b0), .in1(n16_input_register_increment_1_out_30), .in2(n16_input_register_decrement_1_out_29),
    .in3(in_3[13]), .out(multiplexer_14_out), .sel(in_1), .en(in_2));
  Multiplexer #(.select(2)) multiplexer_15 (
    .in0(1'b0), .in1(n16_input_register_increment_1_out_31), .in2(n16_input_register_decrement_1_out_30),
    .in3(in_3[14]), .out(multiplexer_15_out), .sel(in_1), .en(in_2));
  Multiplexer #(.select(2)) multiplexer_16 (
    .in0(1'b0), .in1(n16_input_register_increment_1_out_32), .in2(n16_input_register_decrement_1_out_31),
    .in3(in_3[15]), .out(multiplexer_16_out), .sel(in_1), .en(in_2));
  Clock clock_1 (.out(clock_1_out));
  D_Flip_Flop d_ff_1 (.clk(clock_1_out), .D(multiplexer_1_out), .Q(out_4[0]), .en(in_2));  // open: Qn, preset, reset
  D_Flip_Flop d_ff_2 (.clk(clock_1_out), .D(multiplexer_2_out), .Q(out_4[1]), .en(in_2));  // open: Qn, preset, reset
  D_Flip_Flop d_ff_3 (.clk(clock_1_out), .D(multiplexer_3_out), .Q(out_4[2]), .en(in_2));  // open: Qn, preset, reset
  D_Flip_Flop d_ff_4 (.clk(clock_1_out), .D(multiplexer_4_out), .Q(out_4[3]), .en(in_2));  // open: Qn, preset, reset
  D_Flip_Flop d_ff_5 (.clk(clock_1_out), .D(multiplexer_5_out), .Q(out_4[4]), .en(in_2));  // open: Qn, preset, reset
  D_Flip_Flop d_ff_6 (.clk(clock_1_out), .D(multiplexer_6_out), .Q(out_4[5]), .en(in_2));  // open: Qn, preset, reset
  D_Flip_Flop d_ff_7 (.clk(clock_1_out), .D(multiplexer_7_out), .Q(out_4[6]), .en(in_2));  // open: Qn, preset, reset
  D_Flip_Flop d_ff_8 (.clk(clock_1_out), .D(multiplexer_8_out), .Q(out_4[7]), .en(in_2));  // open: Qn, preset, reset
  D_Flip_Flop d_ff_9 (.clk(clock_1_out), .D(multiplexer_9_out), .Q(out_4[8]), .en(in_2));  // open: Qn, preset, reset
  D_Flip_Flop d_ff_10 (.clk(clock_1_out), .D(multiplexer_10_out), .Q(out_4[9]), .en(in_2));  // open: Qn, preset, reset
  D_Flip_Flop d_ff_11 (.clk(clock_1_out), .D(multiplexer_11_out), .Q(out_4[10]), .en(in_2));  // open: Qn, preset, reset
  D_Flip_Flop d_ff_12 (.clk(clock_1_out), .D(multiplexer_12_out), .Q(out_4[11]), .en(in_2));  // open: Qn, preset, reset
  D_Flip_Flop d_ff_13 (.clk(clock_1_out), .D(multiplexer_13_out), .Q(out_4[12]), .en(in_2));  // open: Qn, preset, reset
  D_Flip_Flop d_ff_14 (.clk(clock_1_out), .D(multiplexer_14_out), .Q(out_4[13]), .en(in_2));  // open: Qn, preset, reset
  D_Flip_Flop d_ff_15 (.clk(clock_1_out), .D(multiplexer_15_out), .Q(out_4[14]), .en(in_2));  // open: Qn, preset, reset
  D_Flip_Flop d_ff_16 (.clk(clock_1_out), .D(multiplexer_16_out), .Q(out_4[15]), .en(in_2));  // open: Qn, preset, reset
endmodule

module _8_bit_Register_File (
  input  [7:0] in_1,
  input  [1:0] OutASel,
  input  [3:0] RegSel,
  input  [1:0] FunSel,
  input  [1:0] OutBSel,
  output [7:0] out_6,
  output [7:0] out_7
);

  wire [7:0] n8_bit_register_1_out_5, n8_bit_register_2_out_5, n8_bit_register_3_out_5,
       n8_bit_register_4_out_5;

  _8_bit_register u_8_bit_register_1 (
    .out_5(n8_bit_register_1_out_5), .in_3(FunSel), .in_4(in_1), .in_2(RegSel[3]));  // open: in_1
  _8_bit_register u_8_bit_register_2 (
    .out_5(n8_bit_register_2_out_5), .in_3(FunSel), .in_4(in_1), .in_2(RegSel[2]));  // open: in_1
  _8_bit_register u_8_bit_register_3 (
    .out_5(n8_bit_register_3_out_5), .in_3(FunSel), .in_4(in_1), .in_2(RegSel[1]));  // open: in_1
  _8_bit_register u_8_bit_register_4 (
    .out_5(n8_bit_register_4_out_5), .in_3(FunSel), .in_4(in_1), .in_2(RegSel[0]));  // open: in_1
  Multiplexer #(.select(2), .width(8)) multiplexer_1 (
    .in0(n8_bit_register_1_out_5), .in1(n8_bit_register_2_out_5), .in2(n8_bit_register_3_out_5),
    .in3(n8_bit_register_4_out_5), .out(out_6), .sel(OutASel), .en(1'b1));
  Multiplexer #(.select(2), .width(8)) multiplexer_2 (
    .in0(n8_bit_register_1_out_5), .in1(n8_bit_register_2_out_5), .in2(n8_bit_register_3_out_5),
    .in3(n8_bit_register_4_out_5), .out(out_7), .sel(OutBSel), .en(1'b1));

  // Notes on the sheet:
  //   R0
  //   R1
  //   R2
  //   R3
endmodule

module Part_2b (
  input  [7:0] in_1,
  input  [1:0] OutCSel,
  input  [2:0] RegSel,
  input  [1:0] FunSel,
  output [7:0] out_5
);

  wire [7:0] n8_bit_register_1_out_5, n8_bit_register_2_out_5, n8_bit_register_3_out_5;

  _8_bit_register u_8_bit_register_1 (
    .out_5(n8_bit_register_1_out_5), .in_3(FunSel), .in_4(in_1), .in_2(RegSel[0]));  // open: in_1
  _8_bit_register u_8_bit_register_2 (
    .out_5(n8_bit_register_2_out_5), .in_3(FunSel), .in_4(in_1), .in_2(RegSel[1]));  // open: in_1
  _8_bit_register u_8_bit_register_3 (
    .out_5(n8_bit_register_3_out_5), .in_3(FunSel), .in_4(in_1), .in_2(RegSel[2]));  // open: in_1
  Multiplexer #(.select(2), .width(8)) multiplexer_1 (
    .in0(n8_bit_register_1_out_5), .in1(n8_bit_register_1_out_5), .in2(n8_bit_register_2_out_5),
    .in3(n8_bit_register_3_out_5), .out(out_5), .sel(OutCSel), .en(1'b1));

  // Notes on the sheet:
  //   PC
  //   AR
  //   SP
endmodule

module _16_bit_IR_Register (
  input  L_H,
  input  [1:0] in_2,
  input  in_3,
  input  [7:0] Input,
  output [15:0] out_5
);

  wire [7:0] undriven;
  wire [15:0] multiplexer_1_out;
  wire [15:8] undriven_2;

  Multiplexer #(.width(16), .enable("false")) multiplexer_1 (
    .in0({Input, undriven}), .in1({undriven_2, Input}), .out(multiplexer_1_out), .sel(L_H));
  _16_bit__register u_16_bit_register_1 (.in_1(in_2), .in_2(in_3), .out_4(out_5), .in_3(multiplexer_1_out));
endmodule
